# Fritzing sketch Alpine funky breakout vM0.01 (saved by Fritzing 0.9.3b)
circuit board: 3.5cm x 2.6cm

parts:
  JS1 = 4-directional Stick Switch with encoder [package=THT]
  J1 = female pin header, 8 pins [form="♀ (female)"]
  5K = Resistor [tolerance=±5% resistance=5k package=THT]
  10K = Resistor [tolerance=±5% resistance=10k package=THT]
  22K = Resistor [tolerance=±5% resistance=22k package=THT]
  33K = Resistor [tolerance=±5% resistance=33k package=THT]
  10K_2 = Resistor [tolerance=±5% resistance=10k package=THT]
  J2 = female pin header, 5 pins [form="♀ (female)"]
  10nF = Capacitor [part_number=10nF package=cap-pth-5mm]
  10nF_2 = Capacitor [part_number=10nF package=cap-pth-5mm]

nets:
  N1: JS1.A, J1.pin4, 5K.Pin_1
  N2: JS1.B, J1.pin5, 10K.Pin_1
  N3: JS1.C, J1.pin6, 22K.Pin_1
  N4: JS1.D, J1.pin7, 33K.Pin_1
  N5: JS1.Push, J1.pin8
  N6: JS1.Com, JS1.GND, JS1.Enc_Com, J1.pin3, J2.pin1, 10nF.2, 10nF_2.1
  N7: JS1.Enc_A, J1.pin1, J2.pin5, 10nF_2.2
  N8: JS1.Enc_B, J1.pin2, J2.pin4, 10nF.1
  N9: 5K.Pin_0, 10K.Pin_0, 22K.Pin_0, 33K.Pin_0, 10K_2.Pin_0, J2.pin3
  N10: 10K_2.Pin_1, J2.pin2

notes:
  GND
  VCC
  ANA
  ENB
  ENA
  A
  B
  C
  D
  PSH
  RKJXT1F42001
  Funky_AL
  vM0.01

custom parts:
  4-directional Stick Switch with encoder: Switch type joystick and encoder from ALPS RKJXT1F42001
