# Fritzing sketch RS16 breakout vM0.01 (saved by Fritzing 1.0.1rc)
circuit board: 4.33772cm x 2.25004cm

parts:
  RS16 = RS16
  R1 = Resistor [tolerance=±5% resistance=10k power=0.25W package=THT]
  J3 = female pin header, 3 pins [form="♀ (female)"]
  R2 = Resistor [tolerance=±5% resistance=10k power=0.25W package=THT]
  R3 = Resistor [tolerance=±5% resistance=10k power=0.25W package=THT]
  R4 = Resistor [tolerance=±5% resistance=10k power=0.25W package=THT]
  R5 = Resistor [tolerance=±5% resistance=10k power=0.25W package=THT]
  R6 = Resistor [tolerance=±5% resistance=10k power=0.25W package=THT]
  R7 = Resistor [tolerance=±5% resistance=10k power=0.25W package=THT]
  RS16_2 = RS16
  R8 = Resistor [tolerance=±5% resistance=10k power=0.25W package=THT]
  R9 = Resistor [tolerance=±5% resistance=10k power=0.25W package=THT]
  R10 = Resistor [tolerance=±5% resistance=10k power=0.25W package=THT]
  R11 = Resistor [tolerance=±5% resistance=10k power=0.25W package=THT]
  R12 = Resistor [tolerance=±5% resistance=10k power=0.25W package=THT]
  R13 = Resistor [tolerance=±5% resistance=10k power=0.25W package=THT]
  R14 = Resistor [tolerance=±5% resistance=10k power=0.25W package=THT]
  J4 = female pin header, 1 pin [form="♀ (female)"]
  J5 = female pin header, 1 pin [form="♀ (female)"]
  J6 = female pin header, 1 pin [form="♀ (female)"]

nets:
  N1: RS16.1, R1.Pin_0, J3.pin3
  N2: RS16.2, R1.Pin_1, R3.Pin_0
  N3: RS16.3, R3.Pin_1, R4.Pin_0
  N4: RS16.4, R2.Pin_0, R4.Pin_1
  N5: RS16.5, R2.Pin_1, R7.Pin_1
  N6: RS16.6, R6.Pin_1, R7.Pin_0
  N7: RS16.7, R5.Pin_1, R6.Pin_0
  N8: RS16.8, J3.pin1, R5.Pin_0, RS16_2.8, R9.Pin_0, J4.pin1
  N9: RS16.COM, J3.pin2, RS16_2.COM, J6.pin1
  N10: RS16_2.1, R8.Pin_0, J5.pin1
  N11: RS16_2.2, R8.Pin_1, R10.Pin_0
  N12: RS16_2.3, R10.Pin_1, R13.Pin_0
  N13: RS16_2.4, R12.Pin_0, R13.Pin_1
  N14: RS16_2.5, R11.Pin_1, R12.Pin_1
  N15: RS16_2.6, R11.Pin_0, R14.Pin_1
  N16: RS16_2.7, R9.Pin_1, R14.Pin_0

notes:
  SIG
  VCC
  GND
  G
  V
  S
  RS16_AL
  vM0.01

custom parts:
  RS16: ROtary switch
