# Fritzing sketch F_Int_AL_HW_v0.05_ATMEGA328P (saved by Fritzing 1.0.1rc)
circuit board: 1.72082cm x 3.65516cm

parts:
  Wheel_in = female pin header, 12 pins [form="♀ (female)"]
  ATMEGA328P = atmega328 [package=dip]
  XTAL2 = Crystal [frequency="16 Mhz" package=THT]
  C2 = Capacitor [package=cap-pth-small-kit]
  C3 = Capacitor [package=cap-pth-small-kit]
  R1 = Resistor [tolerance=±5% power=0.25W resistance=10k package=THT]
  LED1 = LED - 5mm [color="Red (633nm)" current=0.030A package="5 mm [THT]"]
  R2 = Resistor [tolerance=±5% power=0.25W resistance=100 package=THT]
  ICSP = double row female pin header, 6 pins [form="♀ (female)"]

nets:
  N1: Wheel_in.pin3, ATMEGA328P.VCC, ATMEGA328P.AVCC, ATMEGA328P.AREF, R1.Pin_0, ICSP.pin1
  N2: Wheel_in.pin4, Wheel_in.pin5, ATMEGA328P.GND, C2.2, C3.1, LED1.cathode, ICSP.pin3
  N3: Wheel_in.pin6, ATMEGA328P.D12, ICSP.pin6
  N4: Wheel_in.pin7, ATMEGA328P.D11_(PWM), ICSP.pin2
  N5: Wheel_in.pin8, ATMEGA328P.D13, R2.Pin_0, ICSP.pin5
  N6: Wheel_in.pin9, ATMEGA328P.D2, ATMEGA328P.D10_(PWM)
  N7: ATMEGA328P.RESET, R1.Pin_1, ICSP.pin4
  N8: ATMEGA328P.XLAT1, XTAL2.pin_1, C2.1
  N9: ATMEGA328P.XLAT2, XTAL2.pin_0, C3.2
  N10: LED1.anode, R2.Pin_1

notes:
  USB GND
  CS
  CLK
  MOSI
  MISO
  GND
  +3,3V
  +5V
  USB +5V
  Wheel Base connector
  Data+
  Data-
  5V
  3V
  GD
  MI
  CK
  MO
  3
  2
  1
  5
  6
  4
