# Fritzing sketch F_Int_AL_HW_v0.05_ATMEGA_He (saved by Fritzing 1.0.1rc)
circuit board: 2.34371cm x 3.66cm

parts:
  Wheel_in = female pin header, 12 pins [form="♀ (female)"]
  ATMEGA328P = atmega328 [package=dip]
  XTAL2 = Crystal [frequency="16 Mhz" package=THT]
  C2 = Capacitor [package=cap-pth-small-kit]
  C3 = Capacitor [package=cap-pth-small-kit]
  R1 = Resistor [tolerance=±5% power=0.25W resistance=10k package=THT]
  LED1 = LED - 5mm [color="Red (633nm)" current=0.030A package="5 mm [THT]"]
  R2 = Resistor [tolerance=±5% power=0.25W resistance=100 package=THT]
  ICSP = double row female pin header, 6 pins [form="♀ (female)"]
  ICSP1 = female pin header, 14 pins [form="♀ (female)"]
  ICSP2 = female pin header, 14 pins [form="♀ (female)"]

nets:
  N1: Wheel_in.pin3, ATMEGA328P.VCC, ATMEGA328P.AVCC, ATMEGA328P.AREF, R1.Pin_0, ICSP.pin1, ICSP1.pin14, ICSP2.pin6
  N2: Wheel_in.pin4, Wheel_in.pin5, ATMEGA328P.GND, C2.2, C3.1, LED1.cathode, ICSP.pin3, ICSP1.pin2, ICSP1.pin4, ICSP1.pin6, ICSP1.pin8, ICSP1.pin10, ICSP1.pin12, ICSP2.pin1, ICSP2.pin3, ICSP2.pin5, ICSP2.pin7, ICSP2.pin9, ICSP2.pin11, ICSP2.pin13
  N3: Wheel_in.pin6, ATMEGA328P.D12, ICSP.pin6
  N4: Wheel_in.pin7, ATMEGA328P.D11_(PWM), ICSP.pin2
  N5: Wheel_in.pin8, ATMEGA328P.D13, R2.Pin_0, ICSP.pin5
  N6: Wheel_in.pin9, ATMEGA328P.D2, ATMEGA328P.D10_(PWM)
  N7: ATMEGA328P.RESET, R1.Pin_1, ICSP.pin4
  N8: ATMEGA328P.D3_(PWM), ICSP2.pin2
  N9: ATMEGA328P.D4, ICSP2.pin4
  N10: ATMEGA328P.XLAT1, XTAL2.pin_1, C2.1
  N11: ATMEGA328P.XLAT2, XTAL2.pin_0, C3.2
  N12: ATMEGA328P.D5_(PWM), ICSP2.pin8
  N13: ATMEGA328P.D6_(PWM), ICSP2.pin10
  N14: ATMEGA328P.D7, ICSP2.pin12
  N15: ATMEGA328P.D8, ICSP2.pin14
  N16: ATMEGA328P.D9_(PWM), ICSP1.pin13
  N17: ATMEGA328P.A0, ICSP1.pin11
  N18: ATMEGA328P.A1, ICSP1.pin9
  N19: ATMEGA328P.A2, ICSP1.pin7
  N20: ATMEGA328P.A3, ICSP1.pin5
  N21: ATMEGA328P.A4, ICSP1.pin3
  N22: ATMEGA328P.A5, ICSP1.pin1
  N23: LED1.anode, R2.Pin_1

notes:
  USB GND
  CS
  CLK
  MOSI
  MISO
  GND
  +3,3V
  +5V
  USB +5V
  Wheel Base connector
  Data+
  Data-
  5V
  3V
  GD
  MI
  CK
  MO
  D3
  3
  2
  1
  5
  6
  4
  D4
  VCC
  D5
  A3
  A2
  A4
  A5
  D9
  A0
  A1
  D8
  D7
  D6
