# Fritzing sketch F_Int_AL_HW_v0.05_ATTINY85 (saved by Fritzing 1.0.1rc)
circuit board: 3.04002cm x 5.79552cm

parts:
  ATTINY = attiny85 [package=dip]
  BTN = female pin header, 2 pins [form="♀ (female)"]
  10K = Resistor [tolerance=±5% power=0.25W resistance=10k package=THT]
  J4 = double row female pin header, 8 pins [form="♀ (female)"]
  ICSP = double row female pin header, 6 pins [form="♀ (female)"]
  5V = female pin header, 2 pins [form="♀ (female)"]
  Fanatec_Wheelbase_1mm = Fanatec Wheelbase connector
  Fanatec_Wheelbase2mm = Fanatec Wheelbase connector 2mm
  USB = female pin header, 4 pins [form="♀ (female)"]
  J6 = female pin header, 7 pins [form="♀ (female)"]
  USB_2 = female pin header, 4 pins [form="♀ (female)"]

nets:
  N1: ATTINY.Pin_1, 10K.Pin_0, J4.pin3, ICSP.pin3
  N2: ATTINY.Pin_2, BTN.pin1
  N3: ATTINY.Pin_3, Fanatec_Wheelbase2mm.8_-_CS
  N4: ATTINY.Pin_4, BTN.pin2, J4.pin6, ICSP.pin4, 5V.pin1, Fanatec_Wheelbase2mm.3_-_GND, Fanatec_Wheelbase2mm.5_-_GND
  N5: ATTINY.Pin_5, J4.pin7, ICSP.pin5, Fanatec_Wheelbase2mm.2_-_MOSI
  N6: ATTINY.Pin_6, J4.pin1, ICSP.pin1, Fanatec_Wheelbase2mm.1_-_MISO
  N7: ATTINY.Pin_7, J4.pin2, ICSP.pin2, Fanatec_Wheelbase2mm.6_-_CLK
  N8: ATTINY.Pin_8, 10K.Pin_1, J4.pin8, ICSP.pin6, Fanatec_Wheelbase2mm.7_-_3V3
  N9: J4.pin4, 5V.pin2, Fanatec_Wheelbase2mm.4_-_5V
  N10: Fanatec_Wheelbase_1mm.1_-_MISO, J6.pin4
  N11: Fanatec_Wheelbase_1mm.2_-_MOSI, J6.pin5
  N12: Fanatec_Wheelbase_1mm.3_-_GND, Fanatec_Wheelbase_1mm.5_-_GND, J6.pin3
  N13: Fanatec_Wheelbase_1mm.4_-_5V, J6.pin1
  N14: Fanatec_Wheelbase_1mm.6_-_CLK, J6.pin6
  N15: Fanatec_Wheelbase_1mm.7_-_3V3, J6.pin2
  N16: Fanatec_Wheelbase_1mm.8_-_CS, J6.pin7
  N17: Fanatec_Wheelbase_1mm.9_-_USB_5V, USB_2.pin4
  N18: Fanatec_Wheelbase_1mm.11_-_D+, USB_2.pin3
  N19: Fanatec_Wheelbase_1mm.12_-_USB_GND, USB_2.pin1
  N20: Fanatec_Wheelbase_1mm.13_-_D-, USB_2.pin2
  N21: Fanatec_Wheelbase2mm.9_-_USB_5V, USB.pin4
  N22: Fanatec_Wheelbase2mm.11_-_D+, USB.pin3
  N23: Fanatec_Wheelbase2mm.12_-_USB_GND, USB.pin1
  N24: Fanatec_Wheelbase2mm.13_-_D-, USB.pin2

notes:
  FFB
  1
  6
  12
  2
  13
  9
  11
  4
  3
  7
  8
  5
  1  2  3  4
  8  7  6  5
  v0.01
  RST
  GND
  VCC
  5V
  ATTINY
  USB 5V
  D+
  D-
  USB GND
  unlocker
  CS
  CLK
  MOSI
  MISO
  3V3
  Base side
  Wheel side
  Base
  side
  Wheel

custom parts:
  Fanatec Wheelbase connector 2mm: Fanatec Wheelbase connector
