# Fritzing sketch F_Int_AL_HW_v0.05_Nano (saved by Fritzing 1.0.1rc)
circuit board: 1.89185cm x 4.83607cm

parts:
  Wheel_in = female pin header, 12 pins [form="♀ (female)"]
  Composant2 = Arduino Nano (Rev3.0)
  D1 = Rectifier Diode [part_number=1N4001 package="300 mil [THT]"]
  S1 = Step up voltage regulator AL2 [package=THT]

nets:
  N1: Wheel_in.pin3, S1.IN+
  N2: Wheel_in.pin4, Wheel_in.pin5, Composant2.GND, S1.IN-, S1.OUT-
  N3: Wheel_in.pin6, D1.cathode
  N4: Wheel_in.pin7, Composant2.D11/MOSI
  N5: Wheel_in.pin8, Composant2.D13/SCK
  N6: Wheel_in.pin9, Composant2.D2, Composant2.D10
  N7: Composant2.D12/MISO, D1.anode
  N8: Composant2.5V, S1.OUT+

notes:
  USB GND
  CS
  CLK
  MOSI
  MISO
  GND
  +3,3V
  +5V
  USB +5V
  Wheel Base connector
  5V
  3V3
  D+
  D-
  Voltage
  Regulator
  1N4001
  F_FFB_Unlocker_AL
  vM0.01
  USB

custom parts:
  Step up voltage regulator AL2: Toggle Switch
