# Fritzing sketch F_Int_AL_HW_v0.05_Nano_Header (saved by Fritzing 1.0.1rc)
circuit board: 2.5526cm x 4.84054cm

parts:
  Wheel_in = female pin header, 12 pins [form="♀ (female)"]
  Composant2 = Arduino Nano (Rev3.0)
  D1 = Rectifier Diode [part_number=1N4001 package="300 mil [THT]"]
  S1 = Step up voltage regulator AL2 [package=THT]
  J1 = female pin header, 18 pins [form="♀ (female)"]
  J2 = female pin header, 17 pins [form="♀ (female)"]
  RST = female pin header, 2 pins [form="♀ (female)"]

nets:
  N1: Wheel_in.pin3, S1.IN+
  N2: Wheel_in.pin4, Wheel_in.pin5, Composant2.GND, S1.IN-, S1.OUT-, J1.pin1, J1.pin3, J1.pin5, J1.pin7, J1.pin9, J1.pin11, J1.pin13, J1.pin15, J1.pin17, J2.pin2, J2.pin4, J2.pin6, J2.pin8, J2.pin10, J2.pin12, J2.pin14, J2.pin16, RST.pin2
  N3: Wheel_in.pin6, D1.cathode
  N4: Wheel_in.pin7, Composant2.D11/MOSI
  N5: Wheel_in.pin8, Composant2.D13/SCK
  N6: Wheel_in.pin9, Composant2.D2, Composant2.D10
  N7: Composant2.D1/TX, J1.pin2
  N8: Composant2.D0/RX, J1.pin4
  N9: Composant2.RESET, RST.pin1
  N10: Composant2.D3, J1.pin6
  N11: Composant2.D4, J1.pin8
  N12: Composant2.D5, J1.pin10
  N13: Composant2.D6, J1.pin12
  N14: Composant2.D7, J1.pin14
  N15: Composant2.D8, J1.pin16
  N16: Composant2.D9, J1.pin18
  N17: Composant2.D12/MISO, D1.anode
  N18: Composant2.5V, S1.OUT+, J2.pin1
  N19: Composant2.A7, J2.pin3
  N20: Composant2.A6, J2.pin5
  N21: Composant2.A5, J2.pin7
  N22: Composant2.A4, J2.pin9
  N23: Composant2.A3, J2.pin11
  N24: Composant2.A2, J2.pin13
  N25: Composant2.A1, J2.pin15
  N26: Composant2.A0, J2.pin17

notes:
  USB GND
  CS
  CLK
  MOSI
  MISO
  GND
  +3,3V
  +5V
  USB +5V
  Wheel Base connector
  5V
  3V3
  D+
  D-
  Voltage
  Regulator
  1N4001
  F_FFB_Unlocker_AL
  vM0.05_header
  USB
  D0
  D9
  D1
  D3
  D4
  D5
  D6
  D7
  D8
  A1
  A6
  A0
  A2
  A5
  A3
  A4
  A7

custom parts:
  Step up voltage regulator AL2: Toggle Switch
