# Fritzing sketch F_Int_AL_HW_v0.05b_PROMICRO_BOX (saved by Fritzing 1.0.1rc)
circuit board: 8.9cm x 17.1cm

parts:
  ENC3 = ENCODER_2LED [package=encoder_led_2]
  ENC2 = ENCODER_2LED [package=encoder_led_2]
  5V1 = female pin header, 2 pins [form="♀ (female)"]
  J12 = female pin header, 3 pins [form="♀ (female)"]
  RS1 = RS16
  R36 = Resistor [tolerance=±5% resistance=10k power=0.25W package=THT]
  R37 = Resistor [tolerance=±5% resistance=10k power=0.25W package=THT]
  R38 = Resistor [tolerance=±5% resistance=10k power=0.25W package=THT]
  R39 = Resistor [tolerance=±5% resistance=10k power=0.25W package=THT]
  R40 = Resistor [tolerance=±5% resistance=10k power=0.25W package=THT]
  R41 = Resistor [tolerance=±5% resistance=10k power=0.25W package=THT]
  R42 = Resistor [tolerance=±5% resistance=10k power=0.25W package=THT]
  R33 = Resistor [tolerance=±5% power=0.25W resistance=10k package=THT]
  J10 = female pin header, 3 pins [form="♀ (female)"]
  R24 = Resistor [tolerance=±5% power=0.25W resistance=10k package=THT]
  R29 = Resistor [tolerance=±5% power=0.25W resistance=10k package=THT]
  R27 = Resistor [tolerance=±5% power=0.25W resistance=10k package=THT]
  R30 = Resistor [tolerance=±5% power=0.25W resistance=10k package=THT]
  J11 = female pin header, 3 pins [form="♀ (female)"]
  R35 = Resistor [tolerance=±5% power=0.25W resistance=10k package=THT]
  R31 = Resistor [tolerance=±5% power=0.25W resistance=10k package=THT]
  R22 = Resistor [tolerance=±5% power=0.25W resistance=10k package=THT]
  RS2 = RS16
  R23 = Resistor [tolerance=±5% power=0.25W resistance=10k package=THT]
  R34 = Resistor [tolerance=±5% power=0.25W resistance=10k package=THT]
  R25 = Resistor [tolerance=±5% power=0.25W resistance=10k package=THT]
  R26 = Resistor [tolerance=±5% power=0.25W resistance=10k package=THT]
  R28 = Resistor [tolerance=±5% power=0.25W resistance=10k package=THT]
  RS3 = RS16
  R32 = Resistor [tolerance=±5% power=0.25W resistance=10k package=THT]
  J13 = female pin header, 5 pins [form="♀ (female)"]
  10K = Resistor [tolerance=±5% resistance=10k power=0.25W package=THT]
  10K_2 = Resistor [tolerance=±5% resistance=10k power=0.25W package=THT]
  10K_3 = Resistor [tolerance=±5% resistance=10k power=0.25W package=THT]
  10K_4 = Resistor [tolerance=±5% resistance=10k power=0.25W package=THT]
  10K_5 = Resistor [tolerance=±5% resistance=10k power=0.25W package=THT]
  10nF = Capacitor [part_number=10nF package=cap-pth-5mm]
  10nF_2 = Capacitor [part_number=10nF package=cap-pth-5mm]
  Composant1 = ws2812b [package="smd 2812b"]
  Composant2 = ws2812b [package="smd 2812b"]
  MCP23018 = MCP23017 I2C I/O Expander
  ARDUINO_PRO_MICRO1 = Arduino Pro Micro (Clone)
  BUT4 = female pin header, 2 pins [form="♀ (female)"]
  BUT5 = female pin header, 2 pins [form="♀ (female)"]
  RST = female pin header, 2 pins [form="♀ (female)"]
  BUT3 = female pin header, 2 pins [form="♀ (female)"]
  BUT2 = female pin header, 2 pins [form="♀ (female)"]
  Composant3 = ws2812b [package="smd 2812b"]
  Composant4 = ws2812b [package="smd 2812b"]
  Composant5 = ws2812b [package="smd 2812b"]
  Composant6 = ws2812b [package="smd 2812b"]
  Composant7 = ws2812b [package="smd 2812b"]
  Composant8 = ws2812b [package="smd 2812b"]
  Composant9 = ws2812b [package="smd 2812b"]
  Composant10 = ws2812b [package="smd 2812b"]
  NPX = female pin header, 3 pins [form="♀ (female)"]
  100 = Resistor [tolerance=±5% power=0.25W resistance=220 package=THT]
  100_2 = Resistor [tolerance=±5% power=0.25W resistance=220 package=THT]
  100_3 = Resistor [tolerance=±5% power=0.25W resistance=220 package=THT]
  100_4 = Resistor [tolerance=±5% power=0.25W resistance=220 package=THT]
  BUT1 = female pin header, 2 pins [form="♀ (female)"]
  ENC_2 = female pin header, 5 pins [form="♀ (female)"]
  ENC_3 = female pin header, 5 pins [form="♀ (female)"]
  10K_6 = Resistor [tolerance=±5% resistance=10k power=0.25W package=THT]
  10K_7 = Resistor [tolerance=±5% resistance=10k power=0.25W package=THT]
  10K_8 = Resistor [tolerance=±5% resistance=10k power=0.25W package=THT]
  10K_9 = Resistor [tolerance=±5% resistance=10k power=0.25W package=THT]
  USB = USB Connectors [package=usb-b-pth-vertical]
  USB_2 = double row female pin header, 4 pins [form="♀ (female)"]
  B24 = BUTTON LED 2 [package=tactile-pth-12mm]
  B35 = BUTTON LED 2 [package=tactile-pth-12mm]
  B33 = BUTTON LED 2 [package=tactile-pth-12mm]
  B34 = BUTTON LED 2 [package=tactile-pth-12mm]
  B16 = BUTTON LED 2 [package=tactile-pth-12mm]
  B32 = BUTTON LED 2 [package=tactile-pth-12mm]
  B15 = BUTTON LED 2 [package=tactile-pth-12mm]
  B26 = BUTTON LED 2 [package=tactile-pth-12mm]
  B23 = BUTTON LED 2 [package=tactile-pth-12mm]
  B31 = BUTTON LED 2 [package=tactile-pth-12mm]
  B12 = BUTTON LED 2 [package=tactile-pth-12mm]
  B36 = BUTTON LED 2 [package=tactile-pth-12mm]
  B13 = BUTTON LED 2 [package=tactile-pth-12mm]
  B11 = BUTTON LED 2 [package=tactile-pth-12mm]
  B25 = BUTTON LED 2 [package=tactile-pth-12mm]
  B14 = BUTTON LED 2 [package=tactile-pth-12mm]
  10 = female pin header, 12 pins [form="♀ (female)"]
  20 = female pin header, 12 pins [form="♀ (female)"]
  30 = female pin header, 12 pins [form="♀ (female)"]
  JS2 = 4-directional Stick Switch with encoder [package=THT]
  Joystick_PS5 = Joystick PS5 AL [package=joystick]

nets:
  N1: ENC3.Button, MCP23018.GPB7, ENC_3.pin4, B31.1, B31.1b, B11.1, B11.1b, 10.pin11, 20.pin11, 30.pin11
  N2: ENC3.GND_Button, MCP23018.GPA2, ENC_3.pin5, B35.2, B35.2b, B33.2, B33.2b, B34.2, B34.2b, B32.2, B32.2b, B31.2, B31.2b, B36.2, B36.2b, 30.pin2, 30.pin4, 30.pin6, 30.pin8, 30.pin10, 30.pin12
  N3: ENC3.A, MCP23018.GPA3, ENC_3.pin1
  N4: ENC3.B, MCP23018.GPA4, ENC_3.pin3
  VSS: ENC3.GND_ENC, ENC2.GND_ENC, 5V1.pin1, J12.pin1, RS1.8, R42.Pin_0, J10.pin1, J11.pin1, R35.Pin_0, RS2.8, R28.Pin_0, RS3.8, J13.pin1, 10nF.1, 10nF_2.2, Composant1.VSS, Composant2.VSS, MCP23018.VSS, MCP23018.A0, MCP23018.A1, MCP23018.A2, ARDUINO_PRO_MICRO1.GND, BUT4.pin2, BUT5.pin2, RST.pin2, BUT3.pin2, BUT2.pin2, Composant3.VSS, Composant4.VSS, Composant5.VSS, Composant6.VSS, Composant7.VSS, Composant8.VSS, Composant9.VSS, Composant10.VSS, NPX.pin1, BUT1.pin2, ENC_2.pin2, ENC_3.pin2, B24.Kathode-, B35.Kathode-, B33.Kathode-, B34.Kathode-, B16.Kathode-, B32.Kathode-, B15.Kathode-, B26.Kathode-, B23.Kathode-, B31.Kathode-, B12.Kathode-, B36.Kathode-, B13.Kathode-, B11.Kathode-, B25.Kathode-, B14.Kathode-, JS2.Com, JS2.GND, JS2.Enc_Com, Joystick_PS5.SEL-, Joystick_PS5.H-, Joystick_PS5.V-
  N5: ENC2.Button, MCP23018.GPB6, ENC_2.pin5, B32.1, B32.1b, B12.1, B12.1b
  N6: ENC2.GND_Button, MCP23018.GPA1, ENC_2.pin4, B24.2, B24.2b, B26.2, B26.2b, B23.2, B23.2b, B25.2, B25.2b, 20.pin2, 20.pin4, 20.pin6, 20.pin8, 20.pin10, 20.pin12
  N7: ENC2.A, MCP23018.GPB0, ENC_2.pin3
  N8: ENC2.B, MCP23018.GPB1, ENC_2.pin1
  VDD: 5V1.pin2, J12.pin3, RS1.1, R36.Pin_0, J10.pin3, R29.Pin_0, J11.pin3, R22.Pin_0, RS2.1, RS3.1, J13.pin2, 10K.Pin_1, Composant1.VDD, Composant2.VDD, MCP23018.VDD, ARDUINO_PRO_MICRO1.VCC, Composant3.VDD, Composant4.VDD, Composant5.VDD, Composant6.VDD, Composant7.VDD, Composant8.VDD, Composant9.VDD, Composant10.VDD, NPX.pin3, 100.Pin_0, 100_2.Pin_0, 100_3.Pin_0, 100_4.Pin_0, Joystick_PS5.V+, Joystick_PS5.H+
  N9: J12.pin2, RS1.COM, ARDUINO_PRO_MICRO1.D6
  N10: RS1.2, R36.Pin_1, R39.Pin_0
  N11: RS1.3, R37.Pin_0, R39.Pin_1
  N12: RS1.4, R37.Pin_1, R38.Pin_0
  N13: RS1.5, R38.Pin_1, R41.Pin_1
  N14: RS1.6, R40.Pin_1, R41.Pin_0
  N15: RS1.7, R40.Pin_0, R42.Pin_1
  N16: R33.Pin_0, R35.Pin_1, RS3.7
  N17: R33.Pin_1, R34.Pin_0, RS3.6
  N18: J10.pin2, RS2.COM, ARDUINO_PRO_MICRO1.D4
  N19: R24.Pin_0, RS2.4, R23.Pin_1
  N20: R24.Pin_1, R27.Pin_1, RS2.5
  N21: R29.Pin_1, RS3.2, R32.Pin_0
  N22: R27.Pin_0, RS2.6, R26.Pin_1
  N23: R30.Pin_0, RS3.3, R32.Pin_1
  N24: R30.Pin_1, R31.Pin_0, RS3.4
  N25: J11.pin2, RS3.COM, ARDUINO_PRO_MICRO1.D8
  N26: R31.Pin_1, R34.Pin_1, RS3.5
  N27: R22.Pin_1, RS2.2, R25.Pin_0
  N28: RS2.3, R23.Pin_0, R25.Pin_1
  N29: RS2.7, R26.Pin_0, R28.Pin_1
  N30: J13.pin3, 10K.Pin_0, 10K_3.Pin_0, 10K_4.Pin_0, 10K_5.Pin_0, ARDUINO_PRO_MICRO1.A3, 10K_6.Pin_0, 10K_8.Pin_0
  N31: J13.pin4, 10nF_2.1, MCP23018.GPA7, JS2.Enc_B
  N32: J13.pin5, 10nF.2, MCP23018.GPA6, JS2.Enc_A
  N33: 10K_2.Pin_0, 10K_7.Pin_1
  N34: 10K_2.Pin_1, JS2.D
  N35: 10K_3.Pin_1, 10K_9.Pin_0
  N36: 10K_4.Pin_1, JS2.B
  N37: 10K_5.Pin_1, 10K_6.Pin_1, JS2.A
  N38: Composant1.DOUT, Composant3.DIN
  N39: Composant1.DIN, Composant2.DOUT
  N40: Composant2.DIN, ARDUINO_PRO_MICRO1.A2, NPX.pin2
  N41: MCP23018.GPB2, B16.1, B16.1b, B26.1, B26.1b, B36.1, B36.1b, 10.pin3, 20.pin3, 30.pin3
  N42: MCP23018.GPB3, B35.1, B35.1b, B15.1, B15.1b, B25.1, B25.1b, 10.pin5, 20.pin5, 30.pin5
  N43: MCP23018.GPB4, B24.1, B24.1b, B34.1, B34.1b, B14.1, B14.1b, 10.pin7, 20.pin7, 30.pin7
  N44: MCP23018.GPB5, B33.1, B33.1b, B23.1, B23.1b, B13.1, B13.1b, 10.pin9, 20.pin9, 30.pin9
  N45: MCP23018.SCL, ARDUINO_PRO_MICRO1.D3
  N46: MCP23018.SDA, ARDUINO_PRO_MICRO1.D2
  N47: MCP23018.RESET, ARDUINO_PRO_MICRO1.RST, RST.pin1
  N48: MCP23018.INTA, ARDUINO_PRO_MICRO1.TXO
  N49: MCP23018.GPA0, B16.2, B16.2b, B15.2, B15.2b, B12.2, B12.2b, B13.2, B13.2b, B11.2, B11.2b, B14.2, B14.2b, 10.pin2, 10.pin4, 10.pin6, 10.pin8, 10.pin10, 10.pin12
  N50: MCP23018.GPA5, 10.pin1, 20.pin1, 30.pin1
  N51: ARDUINO_PRO_MICRO1.RXI, JS2.Push
  N52: ARDUINO_PRO_MICRO1.D7, Joystick_PS5.SEL+
  N53: ARDUINO_PRO_MICRO1.D9, Joystick_PS5.H
  N54: ARDUINO_PRO_MICRO1.D10, Joystick_PS5.V
  N55: ARDUINO_PRO_MICRO1.D16, BUT5.pin1
  N56: ARDUINO_PRO_MICRO1.D14, BUT4.pin1
  N57: ARDUINO_PRO_MICRO1.D15, BUT3.pin1
  N58: ARDUINO_PRO_MICRO1.A0, BUT2.pin1
  N59: ARDUINO_PRO_MICRO1.A1, BUT1.pin1
  N60: Composant3.DOUT, Composant4.DIN
  N61: Composant4.DOUT, Composant5.DIN
  N62: Composant5.DOUT, Composant6.DIN
  N63: Composant6.DOUT, Composant7.DIN
  N64: Composant7.DOUT, Composant8.DIN
  N65: Composant8.DOUT, Composant9.DIN
  N66: Composant9.DOUT, Composant10.DIN
  N67: 100.Pin_1, B35.Anode+, B33.Anode+, B34.Anode+, B36.Anode+
  N68: 100_2.Pin_1, B32.Anode+, B31.Anode+, B12.Anode+, B11.Anode+
  N69: 100_3.Pin_1, B16.Anode+, B15.Anode+, B13.Anode+, B14.Anode+
  N70: 100_4.Pin_1, B24.Anode+, B26.Anode+, B23.Anode+, B25.Anode+
  N71: 10K_7.Pin_0, 10K_8.Pin_1
  N72: 10K_9.Pin_1, JS2.C
  N73: USB.D+, USB_2.pin3
  N74: USB.D-, USB_2.pin4
  N75: USB.GND, USB_2.pin2
  N76: USB.VBUS, USB_2.pin1

notes:
  Changelog v0.05
  - added reset wiring to MCP23017 instead of pullup resistor
  - voltage regulator silkscreen issue corrected- OK
  - Coupe le lien 3v3 entre arduino et regulator ? - OK
  - Missing bridge between encoder rows (violet) - OK
  - 2 different 5V track networks to split between arduino 5V network and wheel base 5V network. They can be reunited in case of external 5V power suply with the 5V_LINK Jumper
  - Added 5V base connector for LED backlight
  - Reduced PCB size to fit through Podium Hub - a lot of rerouting and silk screen labels movement
  - Added version with Arduino pro micro
  RS16_AL
  GND
  VCC
  SIG
  vM0.01
  Funky_AL
  RKJXT1F42001
  ENA
  ENB
  ANA
  B2
  B1
  1
  2
  4
  3
  6
  5
  |
  +5V
  DIN
  VBUS
  D-
  D+
  5V
  10
  20
  30
  USB_SIDE
  Button_Box_AL
  vM0.05
  10K Resistors
  BUT6
  B21
  B22

custom parts:
  ENCODER_2LED: Rotary Encoder w/ button
  RS16: ROtary switch
  MCP23017 I2C I/O Expander: The MCP23017 uses two i2c pins (these can be shared with other i2c devices), and in exchange gives you 16 general purpose pins. You can set each of 16 pins to be input, output, input with a pullup or open drain. There's even the ability to get an interrupt via an external pin when any of the inputs change so you don't have to keep polling the chip.
  BUTTON LED 2: Various NO switches- pushbuttons, reed, etc
  4-directional Stick Switch with encoder: Switch type joystick and encoder from ALPS RKJXT1F42001
  Joystick PS5 AL: Thumb Joystick Joystick commonly found in PS2 controllers. Two pots and a select switch. Footprint proven. Spark Fun Electronics SKU : COM-09032
