# Fritzing sketch F_Int_AL_HW_v0.05b_PROMICRO_Header (saved by Fritzing 1.0.1rc)
circuit board: 2.5526cm x 4.84054cm

parts:
  Wheel_in = female pin header, 12 pins [form="♀ (female)"]
  D1 = Rectifier Diode [part_number=1N4001 package="300 mil [THT]"]
  S1 = Step up voltage regulator AL2 [package=THT]
  J2 = female pin header, 17 pins [form="♀ (female)"]
  Arduino_pro_micro1 = Arduino Pro Micro (Clone)
  J4 = female pin header, 11 pins [form="♀ (female)"]
  RST = female pin header, 2 pins [form="♀ (female)"]
  ICSP = female pin header, 3 pins [form="♀ (female)"]
  ICSP1 = female pin header, 3 pins [form="♀ (female)"]

nets:
  N1: Wheel_in.pin3, S1.IN+
  N2: Wheel_in.pin4, Wheel_in.pin5, S1.IN-, S1.OUT-, J2.pin2, J2.pin4, J2.pin6, J2.pin8, J2.pin10, J2.pin12, J2.pin14, J2.pin16, Arduino_pro_micro1.GND, J4.pin1, J4.pin3, J4.pin5, J4.pin7, J4.pin9, RST.pin2, ICSP.pin3
  N3: Wheel_in.pin6, D1.cathode
  N4: Wheel_in.pin7, Arduino_pro_micro1.D16, ICSP.pin2
  N5: Wheel_in.pin8, Arduino_pro_micro1.D15, ICSP1.pin2
  N6: Wheel_in.pin9, Arduino_pro_micro1.D7
  N7: D1.anode, Arduino_pro_micro1.D14, ICSP1.pin1
  N8: S1.OUT+, Arduino_pro_micro1.VCC, J4.pin11, ICSP.pin1
  N9: J2.pin1, Arduino_pro_micro1.D9
  N10: J2.pin3, Arduino_pro_micro1.D8
  N11: J2.pin5, Arduino_pro_micro1.D6
  N12: J2.pin7, Arduino_pro_micro1.D5
  N13: J2.pin9, Arduino_pro_micro1.D4
  N14: J2.pin11, Arduino_pro_micro1.D3
  N15: J2.pin13, Arduino_pro_micro1.D2
  N16: J2.pin15, Arduino_pro_micro1.RXI
  N17: J2.pin17, Arduino_pro_micro1.TXO
  N18: Arduino_pro_micro1.D10, J4.pin2
  N19: Arduino_pro_micro1.A0, J4.pin4
  N20: Arduino_pro_micro1.A1, J4.pin6
  N21: Arduino_pro_micro1.A2, J4.pin8
  N22: Arduino_pro_micro1.A3, J4.pin10
  N23: Arduino_pro_micro1.RST, RST.pin1, ICSP1.pin3

notes:
  USB GND
  CS
  CLK
  MOSI
  MISO
  GND
  +3,3V
  +5V
  USB +5V
  Wheel Base connector
  5V
  3V3
  D+
  D-
  Voltage
  Regulator
  1N4001
  F_FFB_Unlocker_AL
  vM0.05_header_PROMICRO
  USB
  D10
  A0
  A1
  A2
  A3
  D9
  D1
  D6
  D0
  D2
  D5
  D3
  D4
  D8
  1
  3
  5
  2
  4
  6
  ICSP Connector

custom parts:
  Step up voltage regulator AL2: Toggle Switch
