# Fritzing sketch F_Interface_AL vM0.05_FULL_NANO (saved by Fritzing 1.0.1rc)
circuit board: 7.95628cm x 8.00762cm

parts:
  J2 = female pin header, 12 pins [form="♀ (female)"]
  J3 = female pin header, 12 pins [form="♀ (female)"]
  RS1 = female pin header, 3 pins [form="♀ (female)"]
  RS2 = female pin header, 3 pins [form="♀ (female)"]
  RS3 = female pin header, 3 pins [form="♀ (female)"]
  AxisX = female pin header, 3 pins [form="♀ (female)"]
  AxisY = female pin header, 3 pins [form="♀ (female)"]
  BX = female pin header, 3 pins [form="♀ (female)"]
  NPX = female pin header, 3 pins [form="♀ (female)"]
  I2C = female pin header, 4 pins [form="♀ (female)"]
  3V = female pin header, 2 pins [form="♀ (female)"]
  5V = female pin header, 2 pins [form="♀ (female)"]
  BY = female pin header, 6 pins [form="♀ (female)"]
  ENC3 = female pin header, 5 pins [form="♀ (female)"]
  ENC2 = female pin header, 5 pins [form="♀ (female)"]
  ENC1 = female pin header, 8 pins [form="♀ (female)"]
  TFT = female pin header, 8 pins [form="♀ (female)"]
  RST = female pin header, 3 pins [form="♀ (female)"]
  UART = female pin header, 4 pins [form="♀ (female)"]
  USB = female pin header, 4 pins [form="♀ (female)"]
  Wheel_in = female pin header, 12 pins [form="♀ (female)"]
  Composant2 = Arduino Nano (Rev3.0)
  3V3 = Jumper [package=sj_2s-no]
  5V_2 = Jumper [package=sj_2s-no]
  MISO_3V3 = Jumper [package=sj_2s-no]
  MISO_5V = Jumper [package=sj_2s-no]
  CS_5V = Jumper [package=sj_2s-no]
  BUT = female pin header, 2 pins [form="♀ (female)"]
  MCP23017 = MCP23017 I2C I/O Expander
  D1 = Rectifier Diode [part_number=1N4001 package="300 mil [THT]"]
  J1 = female pin header, 12 pins [form="♀ (female)"]
  S1 = Step up voltage regulator AL2 [package=THT]
  5V_LINK = Jumper [package=sj_2s-no]
  5V_BASE = female pin header, 2 pins [form="♀ (female)"]

nets:
  N1: J2.pin1, J3.pin1, BY.pin1, MCP23017.GPB7, J1.pin1
  N2: J2.pin2, J2.pin4, J2.pin6, J2.pin8, J2.pin10, J2.pin12, BX.pin2, ENC1.pin8, MCP23017.GPA1
  N3: J2.pin3, J3.pin3, BY.pin2, MCP23017.GPB6, J1.pin3
  N4: J2.pin5, J3.pin5, BY.pin3, MCP23017.GPB5, J1.pin5
  N5: J2.pin7, J3.pin7, BY.pin4, MCP23017.GPB4, J1.pin7
  N6: J2.pin9, J3.pin9, BY.pin5, MCP23017.GPB3, J1.pin9
  N7: J2.pin11, J3.pin11, BY.pin6, MCP23017.GPB2, J1.pin11
  N8: J3.pin2, J3.pin4, J3.pin6, J3.pin8, J3.pin10, J3.pin12, BX.pin1, ENC2.pin5, MCP23017.GPA0
  GND: RS1.pin1, RS2.pin1, RS3.pin1, AxisX.pin1, AxisY.pin1, NPX.pin1, I2C.pin4, 3V.pin2, 5V.pin1, ENC3.pin3, ENC2.pin3, ENC1.pin1, ENC1.pin6, TFT.pin1, RST.pin2, UART.pin2, Wheel_in.pin4, Wheel_in.pin5, Composant2.GND, MCP23017.VSS, MCP23017.A0, MCP23017.A1, MCP23017.A2, S1.IN-, S1.OUT-, 5V_BASE.pin2
  N9: RS1.pin2, Composant2.A0
  N10: RS1.pin3, RS2.pin3, RS3.pin3, AxisX.pin3, AxisY.pin3, I2C.pin3, ENC1.pin2, TFT.pin2, UART.pin1, 3V3.1, 5V_2.1, MCP23017.VDD
  N11: RS2.pin2, Composant2.A1
  N12: RS3.pin2, Composant2.A2
  N13: AxisX.pin2, Composant2.A3
  N14: AxisY.pin2, Composant2.A6
  N15: BX.pin3, ENC3.pin5, MCP23017.GPA2, J1.pin2, J1.pin4, J1.pin6, J1.pin8, J1.pin10, J1.pin12
  N16: NPX.pin2, Composant2.D9
  N17: NPX.pin3, TFT.pin8, Wheel_in.pin2, 5V_LINK.1, 5V_BASE.pin1
  N18: I2C.pin1, Composant2.A4, MCP23017.SDA
  N19: I2C.pin2, Composant2.A5, MCP23017.SCL
  N20: 3V.pin1, Wheel_in.pin3, 3V3.2, S1.IN+
  N21: 5V.pin2, Composant2.5V, 5V_2.2, S1.OUT+, 5V_LINK.2
  N22: ENC3.pin1, MCP23017.GPB0
  N23: ENC3.pin2, MCP23017.GPB1
  N24: ENC3.pin4, ENC2.pin4, ENC1.pin7, MCP23017.GPA5
  N25: ENC2.pin1, MCP23017.GPA3
  N26: ENC2.pin2, MCP23017.GPA4
  N27: ENC1.pin3, Composant2.A7
  N28: ENC1.pin4, MCP23017.GPA7
  N29: ENC1.pin5, MCP23017.GPA6
  N30: TFT.pin3, Composant2.D2, CS_5V.1
  N31: TFT.pin4, Composant2.D4
  N32: TFT.pin5, RST.pin1, RST.pin3, Composant2.RESET, MCP23017.RESET
  N33: TFT.pin6, Composant2.D6
  N34: TFT.pin7, Composant2.D5
  N35: UART.pin3, Composant2.D1/TX
  N36: UART.pin4, Composant2.D0/RX
  N37: USB.pin1, Wheel_in.pin12
  N38: USB.pin2, Wheel_in.pin11
  N39: USB.pin3, Wheel_in.pin10
  N40: USB.pin4, Wheel_in.pin1
  N41: Wheel_in.pin6, MISO_3V3.2, D1.cathode
  N42: Wheel_in.pin7, Composant2.D11/MOSI
  N43: Wheel_in.pin8, Composant2.D13/SCK
  N44: Wheel_in.pin9, Composant2.D10, CS_5V.2
  N45: Composant2.D3, MCP23017.INTA
  N46: Composant2.D7, BUT.pin1
  N47: Composant2.D8, BUT.pin2
  N48: Composant2.D12/MISO, MISO_3V3.1, MISO_5V.1
  N49: MISO_5V.2, D1.anode

notes:
  USB GND
  CS
  CLK
  MOSI
  MISO
  GND
  +3,3V
  +5V
  USB +5V
  Wheel Base connector
  S
  +
  AxX
  AxY
  RS1
  RS2
  RS3
  F_Interface_AL
  vM0.04
  |
  6
  5
  4
  3
  2
  1
  10
  20
  30
  -
  5V
  RX
  TX
  B1
  B2
  EA
  EB
  A
  B0
  USB 5V
  USBGND
  3V3
  D+
  D-
  BL
  CL
  DI
  RE
  DC
  VCC
  SDA
  RST
  RS
  Voltage
  Regulator
  SCL
  Changelog v0.05
  - added reset wiring to MCP23017 instead of pullup resistor
  - voltage regulator silkscreen issue corrected- OK
  - Coupe le lien 3v3 entre arduino et regulator ? - OK
  - Missing bridge between encoder rows (violet) - OK
  - 2 different 5V track networks to split between arduino 5V network and wheel base 5V network. They can be reunited in case of external 5V power suply with the 5V_LINK Jumper
  - Added 5V base connector for LED backlight
  - Reduced PCB size to fit through Podium Hub - a lot of rerouting and silk screen labels movement

custom parts:
  MCP23017 I2C I/O Expander: The MCP23017 uses two i2c pins (these can be shared with other i2c devices), and in exchange gives you 16 general purpose pins. You can set each of 16 pins to be input, output, input with a pullup or open drain. There's even the ability to get an interrupt via an external pin when any of the inputs change so you don't have to keep polling the chip.
  Step up voltage regulator AL2: Toggle Switch
