# Fritzing sketch F_Interface_AL vM0.05b_PROMICRO (saved by Fritzing 1.0.1rc)
circuit board: 7.95628cm x 8.00762cm

parts:
  J2 = female pin header, 12 pins [form="♀ (female)"]
  J3 = female pin header, 12 pins [form="♀ (female)"]
  RS1 = female pin header, 3 pins [form="♀ (female)"]
  RS2 = female pin header, 3 pins [form="♀ (female)"]
  RS3 = female pin header, 3 pins [form="♀ (female)"]
  AxisX = female pin header, 3 pins [form="♀ (female)"]
  AxisY = female pin header, 3 pins [form="♀ (female)"]
  BX = female pin header, 3 pins [form="♀ (female)"]
  NPX = female pin header, 3 pins [form="♀ (female)"]
  I2C = female pin header, 4 pins [form="♀ (female)"]
  3V = female pin header, 2 pins [form="♀ (female)"]
  5V = female pin header, 2 pins [form="♀ (female)"]
  BY = female pin header, 6 pins [form="♀ (female)"]
  ENC3 = female pin header, 5 pins [form="♀ (female)"]
  ENC2 = female pin header, 5 pins [form="♀ (female)"]
  ENC1 = female pin header, 8 pins [form="♀ (female)"]
  WHEEL_USB = female pin header, 4 pins [form="♀ (female)"]
  Wheel_in = female pin header, 12 pins [form="♀ (female)"]
  MCP23017 = MCP23017 I2C I/O Expander
  D1 = Rectifier Diode [part_number=1N4001 package="300 mil [THT]"]
  J1 = female pin header, 12 pins [form="♀ (female)"]
  S1 = Step up voltage regulator AL2 [package=THT]
  5V_BASE = female pin header, 2 pins [form="♀ (female)"]
  ARDUINO_PRO_MICRO = Arduino Pro Micro (Clone)
  RST = female pin header, 2 pins [form="♀ (female)"]
  BUT2 = female pin header, 2 pins [form="♀ (female)"]
  BUT1 = female pin header, 2 pins [form="♀ (female)"]
  5V_LINK = Jumper [package=sj_2s-no]
  ICSP2 = female pin header, 3 pins [form="♀ (female)"]
  ICSP = female pin header, 3 pins [form="♀ (female)"]

nets:
  N1: J2.pin1, J3.pin1, BY.pin1, MCP23017.GPB7, J1.pin1
  N2: J2.pin2, J2.pin4, J2.pin6, J2.pin8, J2.pin10, J2.pin12, BX.pin2, ENC1.pin8, MCP23017.GPA1
  N3: J2.pin3, J3.pin3, BY.pin2, MCP23017.GPB6, J1.pin3
  N4: J2.pin5, J3.pin5, BY.pin3, MCP23017.GPB5, J1.pin5
  N5: J2.pin7, J3.pin7, BY.pin4, MCP23017.GPB4, J1.pin7
  N6: J2.pin9, J3.pin9, BY.pin5, MCP23017.GPB3, J1.pin9
  N7: J2.pin11, J3.pin11, BY.pin6, MCP23017.GPB2, J1.pin11
  N8: J3.pin2, J3.pin4, J3.pin6, J3.pin8, J3.pin10, J3.pin12, BX.pin1, ENC2.pin5, MCP23017.GPA0
  VSS: RS1.pin1, RS2.pin1, RS3.pin1, AxisX.pin1, AxisY.pin1, NPX.pin1, I2C.pin4, 3V.pin2, 5V.pin1, ENC3.pin3, ENC2.pin3, ENC1.pin1, ENC1.pin6, Wheel_in.pin4, Wheel_in.pin5, MCP23017.VSS, MCP23017.A0, MCP23017.A1, MCP23017.A2, S1.IN-, S1.OUT-, 5V_BASE.pin2, ARDUINO_PRO_MICRO.GND, RST.pin2, ICSP.pin3
  N9: RS1.pin2, ARDUINO_PRO_MICRO.D4
  VDD: RS1.pin3, RS2.pin3, RS3.pin3, AxisX.pin3, AxisY.pin3, I2C.pin3, 5V.pin2, ENC1.pin2, MCP23017.VDD, S1.OUT+, ARDUINO_PRO_MICRO.VCC, 5V_LINK.2, ICSP.pin1
  N10: RS2.pin2, ARDUINO_PRO_MICRO.D6
  N11: RS3.pin2, ARDUINO_PRO_MICRO.D8
  N12: AxisX.pin2, ARDUINO_PRO_MICRO.D9
  N13: AxisY.pin2, ARDUINO_PRO_MICRO.D10
  N14: BX.pin3, ENC3.pin5, MCP23017.GPA2, J1.pin2, J1.pin4, J1.pin6, J1.pin8, J1.pin10, J1.pin12
  N15: NPX.pin2, ARDUINO_PRO_MICRO.A2
  N16: NPX.pin3, Wheel_in.pin2, 5V_BASE.pin1, 5V_LINK.1
  N17: I2C.pin1, MCP23017.SDA, ARDUINO_PRO_MICRO.D2
  N18: I2C.pin2, MCP23017.SCL, ARDUINO_PRO_MICRO.D3
  N19: 3V.pin1, Wheel_in.pin3, S1.IN+
  N20: ENC3.pin1, MCP23017.GPB0
  N21: ENC3.pin2, MCP23017.GPB1
  N22: ENC3.pin4, ENC2.pin4, ENC1.pin7, MCP23017.GPA5
  N23: ENC2.pin1, MCP23017.GPA3
  N24: ENC2.pin2, MCP23017.GPA4
  N25: ENC1.pin3, ARDUINO_PRO_MICRO.A3
  N26: ENC1.pin4, MCP23017.GPA7
  N27: ENC1.pin5, MCP23017.GPA6
  N28: WHEEL_USB.pin1, Wheel_in.pin12
  N29: WHEEL_USB.pin2, Wheel_in.pin11
  N30: WHEEL_USB.pin3, Wheel_in.pin10
  N31: WHEEL_USB.pin4, Wheel_in.pin1
  N32: Wheel_in.pin6, D1.cathode
  N33: Wheel_in.pin7, ARDUINO_PRO_MICRO.D16, ICSP.pin2
  N34: Wheel_in.pin8, ARDUINO_PRO_MICRO.D15, ICSP2.pin2
  N35: Wheel_in.pin9, ARDUINO_PRO_MICRO.D7
  N36: MCP23017.RESET, ARDUINO_PRO_MICRO.RST, RST.pin1, ICSP2.pin3
  N37: MCP23017.INTA, ARDUINO_PRO_MICRO.TXO
  N38: D1.anode, ARDUINO_PRO_MICRO.D14, ICSP2.pin1
  N39: ARDUINO_PRO_MICRO.RXI, BUT2.pin2
  N40: ARDUINO_PRO_MICRO.D5, BUT2.pin1
  N41: ARDUINO_PRO_MICRO.A0, BUT1.pin1
  N42: ARDUINO_PRO_MICRO.A1, BUT1.pin2

notes:
  USB GND
  CS
  CLK
  MOSI
  MISO
  GND
  +3,3V
  +5V
  USB +5V
  Wheel Base connector
  S
  +
  AxX
  AxY
  RS1
  RS2
  RS3
  F_Interface_AL
  vM0.05_PRO_MICRO
  |
  6
  5
  4
  3
  2
  1
  10
  20
  30
  -
  5V
  B1
  B2
  EA
  EB
  A
  USB 5V
  USBGND
  3V3
  D+
  D-
  vM0.0_PRO_MICRO
  Voltage
  Regulator
  SCL
  SDA
  Changelog v0.05
  - added reset wiring to MCP23017 instead of pullup resistor
  - voltage regulator silkscreen issue corrected- OK
  - Coupe le lien 3v3 entre arduino et regulator ? - OK
  - Missing bridge between encoder rows (violet) - OK
  - 2 different 5V track networks to split between arduino 5V network and wheel base 5V network. They can be reunited in case of external 5V power suply with the 5V_LINK Jumper
  - Added 5V base connector for LED backlight
  - Reduced PCB size to fit through Podium Hub - a lot of rerouting and silk screen labels movement
  - Added version with Arduino pro micro
  A1
  A0
  D5
  D1
  USB
  ICSP Connector

custom parts:
  MCP23017 I2C I/O Expander: The MCP23017 uses two i2c pins (these can be shared with other i2c devices), and in exchange gives you 16 general purpose pins. You can set each of 16 pins to be input, output, input with a pullup or open drain. There's even the ability to get an interrupt via an external pin when any of the inputs change so you don't have to keep polling the chip.
  Step up voltage regulator AL2: Toggle Switch
