# Fritzing sketch F_Interface_AL_Hardware_v0.02 (saved by Fritzing 0.9.3b)
circuit board: 10cm x 6.89999cm

parts:
  Arduino_Nano = Arduino Nano (Rev3.0)
  R51 = Resistor [tolerance=±5% resistance=10k package=THT]
  R52 = Resistor [tolerance=±5% resistance=10k package=THT]
  R53 = Resistor [tolerance=±5% resistance=10k package=THT]
  R54 = Resistor [tolerance=±5% resistance=10k package=THT]
  C11 = Capacitor [part_number=10nF package=cap-pth-5mm]
  C12 = Capacitor [part_number=10nF package=cap-pth-5mm]
  C13 = Capacitor [part_number=10nF package=cap-pth-5mm]
  C14 = Capacitor [part_number=10nF package=cap-pth-5mm]
  R67 = Resistor [tolerance=±5% resistance=100 package=THT]
  R68 = Resistor [tolerance=±5% resistance=100 package=THT]
  R69 = Resistor [tolerance=±5% resistance=100 package=THT]
  R70 = Resistor [tolerance=±5% resistance=100 package=THT]
  C17 = Capacitor [part_number=10nF package=cap-pth-5mm]
  C18 = Capacitor [part_number=10nF package=cap-pth-5mm]
  C19 = Capacitor [part_number=10nF package=cap-pth-5mm]
  C20 = Capacitor [part_number=10nF package=cap-pth-5mm]
  R71 = Resistor [tolerance=±5% resistance=10k package=THT]
  R72 = Resistor [tolerance=±5% resistance=10k package=THT]
  R73 = Resistor [tolerance=±5% resistance=10k package=THT]
  R74 = Resistor [tolerance=±5% resistance=10k package=THT]
  R75 = Resistor [tolerance=±5% resistance=10k package=THT]
  R76 = Resistor [tolerance=±5% resistance=10k package=THT]
  R77 = Resistor [tolerance=±5% resistance=10k package=THT]
  R78 = Resistor [tolerance=±5% resistance=10k package=THT]
  R79 = Resistor [tolerance=±5% resistance=10k package=THT]
  R80 = Resistor [tolerance=±5% resistance=10k package=THT]
  R81 = Resistor [tolerance=±5% resistance=10k package=THT]
  R82 = Resistor [tolerance=±5% resistance=10k package=THT]
  R83 = Resistor [tolerance=±5% resistance=10k package=THT]
  R84 = Resistor [tolerance=±5% resistance=10k package=THT]
  R85 = Resistor [tolerance=±5% resistance=10k package=THT]
  R86 = Resistor [tolerance=±5% resistance=10k package=THT]
  R87 = Resistor [tolerance=±5% resistance=10k package=THT]
  R88 = Resistor [tolerance=±5% resistance=10k package=THT]
  R89 = Resistor [tolerance=±5% resistance=10k package=THT]
  R90 = Resistor [tolerance=±5% resistance=10k package=THT]
  R91 = Resistor [tolerance=±5% resistance=10k package=THT]
  R92 = Resistor [tolerance=±5% resistance=10k package=THT]
  Wheel_in = female pin header, 12 pins [form="♀ (female)"]
  J10 = female pin header, 4 pins [form="♀ (female)"]
  BUT_4 = female pin header, 5 pins [form="♀ (female)"]
  APM_R = female pin header, 6 pins [form="♀ (female)"]
  RS2 = female pin header, 3 pins [form="♀ (female)"]
  BUT_2 = female pin header, 5 pins [form="♀ (female)"]
  J9 = female pin header, 4 pins [form="♀ (female)"]
  ENC_2 = female pin header, 3 pins [form="♀ (female)"]
  RS4 = female pin header, 3 pins [form="♀ (female)"]
  JOY = female pin header, 5 pins [form="♀ (female)"]
  J11 = female pin header, 5 pins [form="♀ (female)"]
  DPAD = female pin header, 7 pins [form="♀ (female)"]
  OLED = female pin header, 4 pins [form="♀ (female)"]
  Reset = female pin header, 2 pins [form="♀ (female)"]
  RS3 = female pin header, 3 pins [form="♀ (female)"]
  BUT_3 = female pin header, 5 pins [form="♀ (female)"]
  J12 = female pin header, 4 pins [form="♀ (female)"]
  APM_L = female pin header, 6 pins [form="♀ (female)"]
  ENC_1 = female pin header, 3 pins [form="♀ (female)"]
  BUT_1 = female pin header, 5 pins [form="♀ (female)"]
  J13 = female pin header, 4 pins [form="♀ (female)"]
  RS1 = female pin header, 3 pins [form="♀ (female)"]
  NPX = female pin header, 3 pins [form="♀ (female)"]
  TM1637 = female pin header, 4 pins [form="♀ (female)"]
  MUX_OUT = female pin header, 16 pins [form="♀ (female)"]
  MUX_IN = female pin header, 8 pins [form="♀ (female)"]
  POWER = female pin header, 2 pins [form="♀ (female)"]
  ICSP = double row female pin header, 6 pins [form="♀ (female)"]
  J15 = female pin header, 6 pins [form="♀ (female)"]
  J16 = female pin header, 6 pins [form="♀ (female)"]
  SUH+ = female pin header, 1 pin [form="♀ (female)"]
  SUH- = female pin header, 1 pin [form="♀ (female)"]
  SUL- = female pin header, 1 pin [form="♀ (female)"]
  SUL+ = female pin header, 1 pin [form="♀ (female)"]
  J14 = female pin header, 6 pins [form="♀ (female)"]
  TFT = female pin header, 8 pins [form="♀ (female)"]

nets:
  N1: Arduino_Nano.GND, C11.2, C12.2, C13.2, C14.2, C17.2, C18.1, C19.2, C20.1, Wheel_in.pin4, Wheel_in.pin5, J10.pin1, J10.pin2, J10.pin3, J10.pin4, BUT_4.pin5, APM_R.pin1, APM_R.pin5, RS2.pin3, BUT_2.pin5, J9.pin1, J9.pin2, J9.pin3, J9.pin4, ENC_2.pin2, RS4.pin3, JOY.pin1, J11.pin1, J11.pin2, J11.pin3, J11.pin4, J11.pin5, DPAD.pin7, OLED.pin4, Reset.pin2, RS3.pin3, BUT_3.pin5, J12.pin1, J12.pin2, J12.pin3, J12.pin4, APM_L.pin1, APM_L.pin5, ENC_1.pin2, BUT_1.pin5, J13.pin1, J13.pin2, J13.pin3, J13.pin4, RS1.pin3, NPX.pin3, TM1637.pin3, MUX_IN.pin6, MUX_IN.pin8, POWER.pin1, ICSP.pin1, J15.pin3, SUH-.pin1, SUL-.pin1, J14.pin1, TFT.pin4
  N2: Arduino_Nano.D2, Arduino_Nano.D10, J16.pin6
  N3: Arduino_Nano.D3, MUX_IN.pin5
  N4: Arduino_Nano.D4, MUX_IN.pin4
  N5: Arduino_Nano.D5, C19.1, ENC_2.pin1
  N6: Arduino_Nano.D6, C20.2, ENC_2.pin3
  N7: Arduino_Nano.D7, MUX_IN.pin3
  N8: Arduino_Nano.D8, MUX_IN.pin2
  N9: Arduino_Nano.D9, NPX.pin1
  N10: Arduino_Nano.D11/MOSI, J16.pin2, TFT.pin6
  N11: Arduino_Nano.D12/MISO, J16.pin1
  N12: Arduino_Nano.RESET, Reset.pin1, TFT.pin1
  N13: Arduino_Nano.5V, R51.Pin_1, R71.Pin_1, R75.Pin_1, R79.Pin_1, R87.Pin_1, R88.Pin_1, R90.Pin_1, R92.Pin_1, APM_R.pin6, RS2.pin1, RS4.pin1, JOY.pin2, DPAD.pin1, OLED.pin3, RS3.pin1, APM_L.pin6, RS1.pin1, NPX.pin2, TM1637.pin4, MUX_IN.pin7, POWER.pin2, ICSP.pin3, J16.pin4, SUH+.pin1, J14.pin5, TFT.pin2, TFT.pin3
  N14: Arduino_Nano.A5, OLED.pin2, TFT.pin8
  N15: Arduino_Nano.A4, OLED.pin1, TM1637.pin1, TFT.pin7
  N16: Arduino_Nano.A3, C18.2, ENC_1.pin3
  N17: Arduino_Nano.A2, C17.1, ENC_1.pin1
  N18: Arduino_Nano.A1, MUX_IN.pin1
  N19: Arduino_Nano.A0, TM1637.pin2
  N20: Arduino_Nano.D13/SCK, J16.pin5, TFT.pin5
  N21: R51.Pin_0, R52.Pin_1, BUT_1.pin4, MUX_OUT.pin15
  N22: R52.Pin_0, R53.Pin_0, BUT_1.pin3
  N23: R53.Pin_1, R54.Pin_0, BUT_1.pin2
  N24: R54.Pin_1, BUT_1.pin1
  N25: C11.1, R67.Pin_0, RS4.pin2
  N26: C12.1, R68.Pin_0, RS3.pin2
  N27: C13.1, R69.Pin_0, RS2.pin2
  N28: C14.1, R70.Pin_0, RS1.pin2
  N29: R67.Pin_1, MUX_OUT.pin6
  N30: R68.Pin_1, MUX_OUT.pin11
  N31: R69.Pin_1, MUX_OUT.pin1
  N32: R70.Pin_1, MUX_OUT.pin16
  N33: R71.Pin_0, R72.Pin_1, BUT_2.pin4, MUX_OUT.pin2
  N34: R72.Pin_0, R74.Pin_0, BUT_2.pin3
  N35: R73.Pin_0, R74.Pin_1, BUT_2.pin2
  N36: R73.Pin_1, BUT_2.pin1
  N37: R75.Pin_0, R76.Pin_1, BUT_3.pin4, MUX_OUT.pin12
  N38: R76.Pin_0, R78.Pin_0, BUT_3.pin3
  N39: R77.Pin_0, R78.Pin_1, BUT_3.pin2
  N40: R77.Pin_1, BUT_3.pin1
  N41: R79.Pin_0, R80.Pin_1, BUT_4.pin4, MUX_OUT.pin5
  N42: R80.Pin_0, R81.Pin_0, BUT_4.pin3
  N43: R81.Pin_1, R82.Pin_0, BUT_4.pin2
  N44: R82.Pin_1, BUT_4.pin1
  N45: R83.Pin_0, R84.Pin_1, DPAD.pin5
  N46: R83.Pin_1, R87.Pin_0, DPAD.pin6, MUX_OUT.pin10
  N47: R84.Pin_0, R85.Pin_0, DPAD.pin4
  N48: R85.Pin_1, R86.Pin_0, DPAD.pin3
  N49: R86.Pin_1, DPAD.pin2
  N50: R88.Pin_0, R89.Pin_0, APM_L.pin3, MUX_OUT.pin13
  N51: R89.Pin_1, APM_L.pin4
  N52: R90.Pin_0, R91.Pin_0, APM_R.pin3, MUX_OUT.pin4
  N53: R91.Pin_1, APM_R.pin4
  N54: R92.Pin_0, JOY.pin5, MUX_OUT.pin7
  N55: Wheel_in.pin3, J15.pin4, SUL+.pin1
  N56: Wheel_in.pin6, J15.pin1
  N57: Wheel_in.pin7, J15.pin2
  N58: Wheel_in.pin8, J15.pin5
  N59: Wheel_in.pin9, J15.pin6
  N60: APM_R.pin2, MUX_OUT.pin3
  N61: JOY.pin3, MUX_OUT.pin9
  N62: JOY.pin4, MUX_OUT.pin8
  N63: APM_L.pin2, MUX_OUT.pin14
  N64: ICSP.pin2, J14.pin3
  N65: ICSP.pin4, J14.pin6
  N66: ICSP.pin5, J14.pin4
  N67: ICSP.pin6, J14.pin2

notes:
  BLink L/R
  Wheel Base connector
  USB +5V
  DIY Steering Wheel
  AL
  2/6/23
  v0.02 changelog :
  - capacitors labels pF --> nF
  - Sensors holes changed to medium size
  - changed pins for ENC_2 to D6 and D5 instead of A6 and A7
  - changed size of ICSP and POWER pins to 2,54mm pitch instead of 2mm pitch
  - Changed PCB holes dimater to fit QR-1 clubsport specs.
  +5V
  +3,3V
  GND
  MISO
  MOSI
  CLK
  CS
  USB GND
  BUTTON GROUP
  TOP RIGHT ROTARY SWITCH
  TOP LEFT ROTARY SWITCH
  Rotary switches
  Encoders
  APM
  DPAD
  MUX_IN
  MUX_OUT
  JOY
  STEP-UP
  Ground pins
  100
  10K
  10nF
  3V3
  5V
  VCC
  DO
  A
  B
  PLD
  PLU
  9
  10
  12
  11
  S
  U
  C
  L
  R
  13
  14
  15
  16
  PDR
  PUR
  APR
  5
  6
  7
  8
  1
  4
  3
  2
  X
  Y
  D
  RST
  F_Interface
  AL vM0.02
  Step up
  Voltage
  Regulator
  CD74HC4067
  Breakout board
  SIG
  C15
  C0
  DIO
  SCL
  SDA
  APL
  (5V)
  (U+)
  Level Shifter
  1  2  3  4
  BUT_1
  BUT_2
  BUT_3
  BUT_4
  5  6  7  8
  9 10 11 12
  13 14 15 16
  U C L D R
  LED
  DC
